# Fritzing sketch Lab1Sch (saved by Fritzing 0.9.4)
breadboards: 1

parts:
  SW1 = DIP Switch 8 Position [package=dipswitch-08]
  U1 = 7400 4 x 2 Input NAND Gate [part_number=7400 package="DIP (Dual Inline) [THT]"]
  LED1 = smd LED [color="Red (633nm)" package="0805 [SMD]"]
  R1 = Resistor [tolerance=±5% resistance=330 package=THT]
  U2 = 7400 4 x 2 Input NAND Gate [part_number=7400 package="DIP (Dual Inline) [THT]"]
  U3 = 7410 3 x 3 Input NAND Gate [part_number=7410 package="DIP (Dual Inline) [THT]"]
  LED2 = smd LED [color="Red (633nm)" package="0805 [SMD]"]
  R2 = Resistor [tolerance=±5% resistance=330 package=THT]
  R3 = Resistor [tolerance=±5% resistance=1k package=THT]
  R4 = Resistor [tolerance=±5% resistance=1k package=THT]
  R5 = Resistor [tolerance=±5% resistance=1k package=THT]

nets:
  N1: SW1.6, U1.Q2, U2.Q2, U2.B3, R5.Pin_0
  N2: SW1.7, U1.A1, U1.B1, U1.B4, U2.A1, U2.B1, U2.A4, R4.Pin_0
  N3: SW1.8, U1.A4, U2.Q3, U2.B4, R3.Pin_0
  3.3V: SW1.9, SW1.10, SW1.11, U1.VDD, U2.VDD, U3.VDD
  N4: U1.Q1, U1.A2
  N5: U1.B2, U1.B3
  GND: U1.GND, R1.Pin_1, U2.GND, U3.GND, R2.Pin_1, R5.Pin_1
  N6: U1.A3, LED1.anode
  N7: U1.Q3, U1.Q4
  N8: U2.Q1, U2.A2
  N9: U2.B2, U3.A1
  N10: U2.A3, U3.B4
  N11: U2.Q4, U3.B1
  N12: U3.A4, LED2.anode

notes:
  A
  B
  C
  Prelab A
  Prelab B
  Z

custom parts:
  7410 3 x 3 Input NAND Gate: 7410 3 x 2 Input NAND Gate
