# Fritzing sketch component (saved by Fritzing 0.9.4)
breadboards: 2

parts:
  U1 = 7400 4 x 2 Input NAND Gate [part_number=7400 package="DIP (Dual Inline) [THT]"]
  U2 = 7400 4 x 2 Input NAND Gate [part_number=7400 package="DIP (Dual Inline) [THT]"]
  U3 = 7410 3 x 3 Input NAND Gate [part_number=7410 package="DIP (Dual Inline) [THT]"]
  SW1 = DIP Switch 8 Position [package=dipswitch-08]
  R1 = Resistor [tolerance=±5% resistance=1k package=THT]
  R2 = Resistor [tolerance=±5% resistance=1k package=THT]
  R3 = Resistor [tolerance=±5% resistance=1k package=THT]
  LED1 = LED - 5mm [color="Red (633nm)" package="5 mm [THT]"]
  R4 = Resistor [tolerance=±5% resistance=330 package=THT]
  SW2 = DIP Switch 8 Position [package=dipswitch-08]
  R5 = Resistor [tolerance=±5% resistance=1k package=THT]
  R6 = Resistor [tolerance=±5% resistance=1k package=THT]
  R7 = Resistor [tolerance=±5% resistance=1k package=THT]
  LED2 = LED - 5mm [color="Red (633nm)" package="5 mm [THT]"]
  R8 = Resistor [tolerance=±5% resistance=330 package=THT]

nets:
  N1: U1.A1, U1.B1, U1.B4, SW1.2, R2.Pin_1
  N2: U1.Q1, U1.A2, U1.B3
  N3: U1.Q2, SW1.3, R3.Pin_1
  N4: U1.GND, R1.Pin_0, R2.Pin_0, R3.Pin_0
  N5: U1.A3, LED1.anode
  N6: U1.Q3, U1.Q4
  N7: U1.A4, SW1.1, R1.Pin_1
  N8: U1.VDD, SW1.14, SW1.15, SW1.16
  N9: U2.A1, U2.B1, U2.A4, SW2.2, R6.Pin_1
  N10: U2.Q1, U2.A2
  N11: U2.Q2, U2.B3, SW2.3, R7.Pin_1
  N12: U2.B2, U3.A1
  GND: U2.GND, U3.GND, R5.Pin_0, R6.Pin_0, R7.Pin_0
  N13: U2.A3, U3.B4
  N14: U2.Q3, U2.B4, SW2.1, R5.Pin_1
  N15: U2.Q4, U3.B1
  VDD: U2.VDD, U3.VDD, SW2.14, SW2.15, SW2.16
  N16: U3.A4, LED2.anode
  N17: LED1.cathode, R4.Pin_0
  N18: LED2.cathode, R8.Pin_0

notes:
  PrelabB
  PrelabA
  A
  B
  C
  Z

custom parts:
  7410 3 x 3 Input NAND Gate: 7410 3 x 2 Input NAND Gate
